// Logisim project Proyecto.circ as structural Verilog
module LATA (
  input  A7,
  input  A6,
  input  A5,
  input  A4,
  input  A3,
  input  A2,
  input  A1,
  input  A0,
  input  B7,
  input  B6,
  input  B5,
  input  B4,
  input  B3,
  input  B2,
  input  B1,
  input  B0,
  input  C7,
  input  C6,
  input  C5,
  input  C4,
  input  C3,
  input  C2,
  input  C1,
  input  C0,
  output S7,
  output S6,
  output S5,
  output S4,
  output S3,
  output S2,
  output S1,
  output S0,
  output P7,
  output P6,
  output P5,
  output P4,
  output P3,
  output P2,
  output P1,
  output P0,
  output G7,
  output G6,
  output G5,
  output G4,
  output G3,
  output G2,
  output G1,
  output G0
);

  wire xor_1_out, xor_3_out, xor_5_out, xor_7_out, xor_9_out, xor_11_out, xor_13_out, xor_15_out;

  xor xor_1 (xor_1_out, A7, B7);
  xor xor_2 (S7, xor_1_out, C7);
  or or_1 (P7, A7, B7);
  and and_1 (G7, A7, B7);
  xor xor_3 (xor_3_out, A6, B6);
  xor xor_4 (S6, xor_3_out, C6);
  or or_2 (P6, A6, B6);
  and and_2 (G6, A6, B6);
  xor xor_5 (xor_5_out, A5, B5);
  xor xor_6 (S5, xor_5_out, C5);
  or or_3 (P5, A5, B5);
  and and_3 (G5, A5, B5);
  xor xor_7 (xor_7_out, A4, B4);
  xor xor_8 (S4, xor_7_out, C4);
  or or_4 (P4, A4, B4);
  and and_4 (G4, A4, B4);
  xor xor_9 (xor_9_out, A3, B3);
  xor xor_10 (S3, xor_9_out, C3);
  or or_5 (P3, A3, B3);
  and and_5 (G3, A3, B3);
  xor xor_11 (xor_11_out, A2, B2);
  xor xor_12 (S2, xor_11_out, C2);
  or or_6 (P2, A2, B2);
  and and_6 (G2, A2, B2);
  xor xor_13 (xor_13_out, A1, B1);
  xor xor_14 (S1, xor_13_out, C1);
  or or_7 (P1, A1, B1);
  and and_7 (G1, A1, B1);
  xor xor_15 (xor_15_out, A0, B0);
  xor xor_16 (S0, xor_15_out, C0);
  or or_8 (P0, A0, B0);
  and and_8 (G0, A0, B0);

  // Notes on the sheet:
  //   FA7
  //   FA6
  //   FA5
  //   FA4
  //   Los C de cada FA son los Cin que están diagramados en el PDF del proyecto, es decir, dependen de los niveles más altos, hay que unirlos cuando estén hechos
  //   FA3
  //   FA2
  //   FA1
  //   FA0
endmodule
